# Fritzing sketch Board1 (saved by Fritzing 0.9.3b)
circuit board: 5cm x 7cm
perfboards: 1

parts:
  nRF24L01 = mystery part, 8 pins [chip_label=nRF24L01 part_number=nRF24L01]
  Arduino_Pro_Mini = Arduino Pro Mini (5V) [part_number="Arduino Pro Mini"]
  Buzzer = Piezo Speaker [part_number=Buzzer]
  +5V = 4 x AAA Battery Mount [part_number=+5V]
  AMS1117 = mystery part, 3 pins [chip_label=AMS part_number=AMS1117]

nets:
  N1: nRF24L01.pin1, Arduino_Pro_Mini.D2
  N2: nRF24L01.pin2, Arduino_Pro_Mini.MOSI
  N3: nRF24L01.pin3, Arduino_Pro_Mini.D5
  N4: nRF24L01.pin4, AMS1117.pin2
  N5: nRF24L01.pin5, Arduino_Pro_Mini.GND, Buzzer.pin1, +5V.-, AMS1117.pin1
  N6: nRF24L01.pin6, Arduino_Pro_Mini.D4
  N7: nRF24L01.pin7, Arduino_Pro_Mini.SCK
  N8: nRF24L01.pin8, Arduino_Pro_Mini.MISO
  N9: Arduino_Pro_Mini.VCC, +5V.+, AMS1117.pin3
  N10: Arduino_Pro_Mini.D3, Buzzer.pin2
